# Fritzing sketch schematic (saved by Fritzing 0.9.0b)
breadboards: 1

parts:
  Part1 = Arduino Pro Mini v13
  U1 = RF-LINK_RX [package=rf-link_rx]
  Q1 = Basic FET N-Channel [package="DPak [SMD]"]
  LEDs_1+_3- = Header 3 [package=1x03-1mm-ra]
  Motion_sensor_1+_2data_3- = Header 3 [package=1x03-1mm-ra]
  12V_Power = Power plug
  R1_10kohm = Resistor [package="2010 [SMD]"]

nets:
  GND: Part1.GND, U1.GND, Q1.source, Motion_sensor_1+_2data_3-.3, 12V_Power.GND, R1_10kohm.Pin_0
  N1: Part1.RAW, LEDs_1+_3-.1, 12V_Power.VCC
  VCC: Part1.VCC, U1.+5V, Motion_sensor_1+_2data_3-.1
  N2: Part1.D10_PWM/SS, Q1.Gate, R1_10kohm.Pin_1
  N3: Part1.D3_PWM, Motion_sensor_1+_2data_3-.2
  N4: Part1.D2, U1.DATA
  N5: Q1.drain, LEDs_1+_3-.3
